// Logisim project Alu_16Bit.circ as structural Verilog: 14 circuits, main circuit sumadorCompleto1Bit
module main (
  input  [2:0] Operation,
  input  [15:0] A,
  input  [15:0] B,
  output [15:0] Result
);

  wire alu_16bits_1_overflow, alu_16bits_1_zero, bcd7_1_a, bcd7_1_b, bcd7_1_c, bcd7_1_d, bcd7_1_e, bcd7_1_f,
       bcd7_1_g, bcd7_2_a, bcd7_2_b, bcd7_2_c, bcd7_2_d, bcd7_2_e, bcd7_2_f, bcd7_2_g, bcd7_3_a, bcd7_3_b,
       bcd7_3_c, bcd7_3_d, bcd7_3_e, bcd7_3_f, bcd7_3_g, bcd7_4_a, bcd7_4_b, bcd7_4_c, bcd7_4_d, bcd7_4_e,
       bcd7_4_f, bcd7_4_g, bcd7_5_a, bcd7_5_b, bcd7_5_c, bcd7_5_d, bcd7_5_e, bcd7_5_f, bcd7_5_g, Signe;
  wire [15:0] C, D, DM, U, UM;

  LED led_1 (.in(Signe));
  ALU_16Bits alu_16bits_1 (
    .A(A), .Operation(Operation), .B(B), .out_4(Result), .Overflow(alu_16bits_1_overflow),
    .Zero(alu_16bits_1_zero));
  BCD7 bcd7_1 (
    .A3(DM[3]), .A2(DM[2]), .A1(DM[1]), .A0(DM[0]), .a(bcd7_1_a), .b(bcd7_1_b), .c(bcd7_1_c), .d(bcd7_1_d),
    .e(bcd7_1_e), .f(bcd7_1_f), .g(bcd7_1_g));
  LED Zero (.in(alu_16bits_1_zero));
  LED Overflow (.in(alu_16bits_1_overflow));
  _7_Segment_Display u_7_segment_display_1 (
    .g(bcd7_1_g), .f(bcd7_1_f), .a(bcd7_1_a), .b(bcd7_1_b), .e(bcd7_1_e), .d(bcd7_1_d), .c(bcd7_1_c));  // open: dp
  BCD7 bcd7_2 (
    .A3(UM[3]), .A2(UM[2]), .A1(UM[1]), .A0(UM[0]), .a(bcd7_2_a), .b(bcd7_2_b), .c(bcd7_2_c), .d(bcd7_2_d),
    .e(bcd7_2_e), .f(bcd7_2_f), .g(bcd7_2_g));
  LED led_2 (.in(Result[14]));
  LED led_3 (.in(Result[15]));
  LED led_4 (.in(Result[13]));
  _7_Segment_Display u_7_segment_display_2 (
    .g(bcd7_2_g), .f(bcd7_2_f), .a(bcd7_2_a), .b(bcd7_2_b), .e(bcd7_2_e), .d(bcd7_2_d), .c(bcd7_2_c));  // open: dp
  LED led_5 (.in(Result[10]));
  LED led_6 (.in(Result[11]));
  LED led_7 (.in(Result[12]));
  BCD7 bcd7_3 (
    .A3(C[3]), .A2(C[2]), .A1(C[1]), .A0(C[0]), .a(bcd7_3_a), .b(bcd7_3_b), .c(bcd7_3_c), .d(bcd7_3_d),
    .e(bcd7_3_e), .f(bcd7_3_f), .g(bcd7_3_g));
  LED led_8 (.in(Result[8]));
  LED led_9 (.in(Result[9]));
  _7_Segment_Display u_7_segment_display_3 (
    .g(bcd7_3_g), .f(bcd7_3_f), .a(bcd7_3_a), .b(bcd7_3_b), .e(bcd7_3_e), .d(bcd7_3_d), .c(bcd7_3_c));  // open: dp
  LED led_10 (.in(Result[5]));
  LED led_11 (.in(Result[7]));
  LED led_12 (.in(Result[6]));
  BCD7 bcd7_4 (
    .A3(D[3]), .A2(D[2]), .A1(D[1]), .A0(D[0]), .a(bcd7_4_a), .b(bcd7_4_b), .c(bcd7_4_c), .d(bcd7_4_d),
    .e(bcd7_4_e), .f(bcd7_4_f), .g(bcd7_4_g));
  LED led_13 (.in(Result[3]));
  LED led_14 (.in(Result[4]));
  LED led_15 (.in(Result[2]));
  _7_Segment_Display u_7_segment_display_4 (
    .g(bcd7_4_g), .f(bcd7_4_f), .a(bcd7_4_a), .b(bcd7_4_b), .e(bcd7_4_e), .d(bcd7_4_d), .c(bcd7_4_c));  // open: dp
  LED led_16 (.in(Result[1]));
  LED led_17 (.in(Result[0]));
  Division division_1 (
    .in_1(Result), .Unidad(U), .Decena(D), .Centena(C), .Unidad_de_Millar(UM), .Decena_de_Millar(DM),
    .Signe(Signe));
  BCD7 bcd7_5 (
    .A3(U[3]), .A2(U[2]), .A1(U[1]), .A0(U[0]), .a(bcd7_5_a), .b(bcd7_5_b), .c(bcd7_5_c), .d(bcd7_5_d),
    .e(bcd7_5_e), .f(bcd7_5_f), .g(bcd7_5_g));
  _7_Segment_Display u_7_segment_display_5 (
    .g(bcd7_5_g), .f(bcd7_5_f), .a(bcd7_5_a), .b(bcd7_5_b), .e(bcd7_5_e), .d(bcd7_5_d), .c(bcd7_5_c));  // open: dp
endmodule

module sumadorCompleto1Bit (
  input  A,
  input  B,
  input  Cin,
  output R,
  output Cout
);

  wire and_1_out, and_2_out, and_3_out, and_4_out, and_5_out, and_6_out, and_7_out, not_1_out, not_2_out,
       not_3_out, not_4_out, not_5_out, not_6_out;

  not not_1 (not_1_out, A);
  not not_2 (not_2_out, B);
  not not_3 (not_3_out, A);
  not not_4 (not_4_out, Cin);
  not not_5 (not_5_out, B);
  not not_6 (not_6_out, Cin);
  and and_1 (and_1_out, B, Cin);
  and and_2 (and_2_out, A, Cin);
  and and_3 (and_3_out, A, B);
  and and_4 (and_4_out, not_1_out, not_2_out, Cin);
  and and_5 (and_5_out, not_3_out, B, not_4_out);
  and and_6 (and_6_out, A, not_5_out, not_6_out);
  and and_7 (and_7_out, A, B, Cin);
  or or_1 (Cout, and_1_out, and_2_out, and_3_out);
  or or_2 (R, and_4_out, and_5_out, and_6_out, and_7_out);
endmodule

module sumadorCompleto1BitOverflow (
  input  A,
  input  B,
  input  Cin,
  output R,
  output Cout,
  output Overflow
);

  wire and_1_out, and_2_out, and_3_out, and_4_out, and_5_out, and_6_out, and_7_out, and_8_out, and_9_out,
       not_1_out, not_2_out, not_3_out, not_4_out, not_5_out, not_6_out, not_7_out, not_8_out, not_9_out;

  not not_1 (not_1_out, A);
  not not_2 (not_2_out, B);
  not not_3 (not_3_out, A);
  not not_4 (not_4_out, Cin);
  not not_5 (not_5_out, B);
  not not_6 (not_6_out, Cin);
  and and_1 (and_1_out, B, Cin);
  and and_2 (and_2_out, A, Cin);
  and and_3 (and_3_out, A, B);
  not not_7 (not_7_out, A);
  not not_8 (not_8_out, B);
  not not_9 (not_9_out, Cin);
  and and_4 (and_4_out, not_1_out, not_2_out, Cin);
  and and_5 (and_5_out, not_3_out, B, not_4_out);
  and and_6 (and_6_out, A, not_5_out, not_6_out);
  and and_7 (and_7_out, A, B, Cin);
  or or_1 (Cout, and_1_out, and_2_out, and_3_out);
  and and_8 (and_8_out, not_7_out, not_8_out, Cin);
  and and_9 (and_9_out, A, B, not_9_out);
  or or_2 (R, and_4_out, and_5_out, and_6_out, and_7_out);
  or or_3 (Overflow, and_8_out, and_9_out);
endmodule

module ALU_1Bit (
  input  Comparation,
  input  A,
  input  B,
  input  Cin,
  input  [2:0] Operation,
  input  Binvert,
  output Result,
  output Cout
);

  wire and_1_out, multiplexer_1_out, not_1_out, not_2_out, or_1_out, sumadorcompleto1bit_1_r;

  Multiplexer #(.enable("false")) multiplexer_1 (.in0(B), .in1(not_1_out), .out(multiplexer_1_out), .sel(Binvert));
  not not_1 (not_1_out, B);
  and and_1 (and_1_out, A, multiplexer_1_out);
  or or_1 (or_1_out, A, multiplexer_1_out);
  sumadorCompleto1Bit sumadorcompleto1bit_1 (
    .A(A), .B(multiplexer_1_out), .Cin(Cin), .R(sumadorcompleto1bit_1_r), .Cout(Cout));
  not not_2 (not_2_out, or_1_out);
  Multiplexer #(.select(3), .enable("false")) multiplexer_2 (
    .in0(Comparation), .in1(sumadorcompleto1bit_1_r), .in2(and_1_out), .in3(or_1_out), .in4(Comparation),
    .in5(sumadorcompleto1bit_1_r), .in6(Comparation), .in7(not_2_out), .out(Result), .sel(Operation));
endmodule

module ALU_1Bit_Overflow (
  input  Comparation,
  input  A,
  input  B,
  input  Cin,
  input  [2:0] Operation,
  input  Binvert,
  output Result,
  output BHigher,
  output Cout,
  output Overflow
);

  wire and_1_out, and_2_out, and_3_out, multiplexer_1_out, not_1_out, not_2_out, or_1_out, or_2_out,
       sumadorcompleto1bitoverflow_1_overflow, sumadorcompleto1bitoverflow_1_r;

  Multiplexer #(.enable("false")) multiplexer_1 (.in0(B), .in1(not_1_out), .out(multiplexer_1_out), .sel(Binvert));
  not not_1 (not_1_out, B);
  and and_1 (and_1_out, A, multiplexer_1_out);
  or or_1 (or_1_out, A, multiplexer_1_out);
  sumadorCompleto1BitOverflow sumadorcompleto1bitoverflow_1 (
    .A(A), .B(multiplexer_1_out), .Cin(Cin), .R(sumadorcompleto1bitoverflow_1_r), .Cout(Cout),
    .Overflow(sumadorcompleto1bitoverflow_1_overflow));
  not not_2 (not_2_out, or_1_out);
  Multiplexer #(.select(3), .enable("false")) multiplexer_2 (
    .in0(Comparation), .in1(sumadorcompleto1bitoverflow_1_r), .in2(and_1_out), .in3(or_1_out),
    .in4(Comparation), .in5(sumadorcompleto1bitoverflow_1_r), .in6(Comparation), .in7(not_2_out),
    .out(Result), .sel(Operation));
  and and_2 (and_2_out, ~Operation[2], ~Operation[1], Operation[0]);  // AND_Gate
  and and_3 (and_3_out, Operation[2], ~Operation[1], Operation[0]);  // AND_Gate
  MYXOR myxor_1 (.A(sumadorcompleto1bitoverflow_1_r), .B(sumadorcompleto1bitoverflow_1_overflow), .XOR(BHigher));
  or or_2 (or_2_out, and_2_out, and_3_out);
  and and_4 (Overflow, or_2_out, sumadorcompleto1bitoverflow_1_overflow);
endmodule

module ALU_16Bits (
  input  [15:0] A,
  input  [2:0] Operation,
  input  [15:0] B,
  output [15:0] out_4,
  output Zero,
  output Overflow
);

  wire alu_1bit_1_cout, alu_1bit_2_cout, alu_1bit_3_cout, alu_1bit_4_cout, alu_1bit_5_cout, alu_1bit_6_cout,
       alu_1bit_7_cout, alu_1bit_9_cout, alu_1bit_10_cout, alu_1bit_11_cout, alu_1bit_12_cout,
       alu_1bit_13_cout, alu_1bit_14_cout, alu_1bit_15_cout, alu_1bit_overflow_1_cout,
       alu_1bit_overflow_1_overflow, BInvert, BMax, Cout8, or_2_out, R0, R1, R2, R3, R4, R5, R6, R7, R8, R9,
       R10, R11, R12, R13, R14, R15, slr_l_1_overflow;
  wire [15:0] SLR;

  Multiplexer #(.select(3), .enable("false")) multiplexer_1 (
    .in0(1'b0), .in1(1'b1), .in2(1'b0), .in3(1'b0), .in4(1'b1), .in5(1'b0), .in6(1'b1), .in7(1'b0),
    .out(BInvert), .sel(Operation));
  ALU_1Bit alu_1bit_1 (
    .Result(R0), .A(A[0]), .B(B[0]), .Cin(BInvert), .Binvert(BInvert), .Cout(alu_1bit_1_cout),
    .Operation(Operation), .Comparation(BMax));
  ALU_1Bit alu_1bit_2 (
    .Result(R1), .A(A[1]), .B(B[1]), .Cin(alu_1bit_1_cout), .Binvert(BInvert), .Cout(alu_1bit_2_cout),
    .Operation(Operation), .Comparation(1'b0));
  ALU_1Bit alu_1bit_3 (
    .Result(R2), .A(A[2]), .B(B[2]), .Cin(alu_1bit_2_cout), .Binvert(BInvert), .Cout(alu_1bit_3_cout),
    .Operation(Operation), .Comparation(1'b0));
  ALU_1Bit alu_1bit_4 (
    .Result(R3), .A(A[3]), .B(B[3]), .Cin(alu_1bit_3_cout), .Binvert(BInvert), .Cout(alu_1bit_4_cout),
    .Operation(Operation), .Comparation(1'b0));
  ALU_1Bit alu_1bit_5 (
    .Result(R4), .A(A[4]), .B(B[4]), .Cin(alu_1bit_4_cout), .Binvert(BInvert), .Cout(alu_1bit_5_cout),
    .Operation(Operation), .Comparation(1'b0));
  ALU_1Bit alu_1bit_6 (
    .Result(R5), .A(A[5]), .B(B[5]), .Cin(alu_1bit_5_cout), .Binvert(BInvert), .Cout(alu_1bit_6_cout),
    .Operation(Operation), .Comparation(1'b0));
  ALU_1Bit alu_1bit_7 (
    .Result(R6), .A(A[6]), .B(B[6]), .Cin(alu_1bit_6_cout), .Binvert(BInvert), .Cout(alu_1bit_7_cout),
    .Operation(Operation), .Comparation(1'b0));
  ALU_1Bit alu_1bit_8 (
    .Result(R7), .A(A[7]), .B(B[7]), .Cin(alu_1bit_7_cout), .Binvert(BInvert), .Cout(Cout8),
    .Operation(Operation), .Comparation(1'b0));
  SLR_L slr_l_1 (.B(B), .in_3(BInvert), .Result(SLR), .A(A), .Overflow(slr_l_1_overflow));
  ALU_1Bit alu_1bit_9 (
    .Result(R8), .A(A[8]), .B(B[8]), .Cin(Cout8), .Binvert(BInvert), .Cout(alu_1bit_9_cout),
    .Operation(Operation), .Comparation(1'b0));
  ALU_1Bit alu_1bit_10 (
    .Result(R9), .A(A[9]), .B(B[9]), .Cin(alu_1bit_9_cout), .Binvert(BInvert), .Cout(alu_1bit_10_cout),
    .Operation(Operation), .Comparation(1'b0));
  ALU_1Bit alu_1bit_11 (
    .Result(R10), .A(A[10]), .B(B[10]), .Cin(alu_1bit_10_cout), .Binvert(BInvert), .Cout(alu_1bit_11_cout),
    .Operation(Operation), .Comparation(1'b0));
  ALU_1Bit alu_1bit_12 (
    .Result(R11), .A(A[11]), .B(B[11]), .Cin(alu_1bit_11_cout), .Binvert(BInvert), .Cout(alu_1bit_12_cout),
    .Operation(Operation), .Comparation(1'b0));
  ALU_1Bit alu_1bit_13 (
    .Result(R12), .A(A[12]), .B(B[12]), .Cin(alu_1bit_12_cout), .Binvert(BInvert), .Cout(alu_1bit_13_cout),
    .Operation(Operation), .Comparation(1'b0));
  ALU_1Bit alu_1bit_14 (
    .Result(R13), .A(A[13]), .B(B[13]), .Cin(alu_1bit_13_cout), .Binvert(BInvert), .Cout(alu_1bit_14_cout),
    .Operation(Operation), .Comparation(1'b0));
  ALU_1Bit alu_1bit_15 (
    .Result(R14), .A(A[14]), .B(B[14]), .Cin(alu_1bit_14_cout), .Binvert(BInvert), .Cout(alu_1bit_15_cout),
    .Operation(Operation), .Comparation(1'b0));
  ALU_1Bit_Overflow alu_1bit_overflow_1 (
    .Result(R15), .A(A[15]), .B(B[15]), .Cin(alu_1bit_15_cout), .Binvert(BInvert),
    .Cout(alu_1bit_overflow_1_cout), .Overflow(alu_1bit_overflow_1_overflow), .Operation(Operation),
    .Comparation(1'b0), .BHigher(BMax));
  or or_1 (Overflow, alu_1bit_overflow_1_overflow, slr_l_1_overflow);
  Multiplexer #(.select(3), .width(16), .enable("false")) multiplexer_2 (
    .in0(SLR), .in1({R15, R14, R13, R12, R11, R10, R9, R8, R7, R6, R5, R4, R3, R2, R1, R0}),
    .in2({R15, R14, R13, R12, R11, R10, R9, R8, R7, R6, R5, R4, R3, R2, R1, R0}),
    .in3({R15, R14, R13, R12, R11, R10, R9, R8, R7, R6, R5, R4, R3, R2, R1, R0}),
    .in4({R15, R14, R13, R12, R11, R10, R9, R8, R7, R6, R5, R4, R3, R2, R1, R0}),
    .in5({R15, R14, R13, R12, R11, R10, R9, R8, R7, R6, R5, R4, R3, R2, R1, R0}), .in6(SLR),
    .in7({R15, R14, R13, R12, R11, R10, R9, R8, R7, R6, R5, R4, R3, R2, R1, R0}), .out(out_4), .sel(Operation));
  or or_2 (or_2_out, out_4[15], out_4[14], out_4[13], out_4[12], out_4[11], out_4[10], out_4[9], out_4[8], out_4[7], out_4[6], out_4[5], out_4[4], out_4[3], out_4[2], out_4[1], out_4[0]);
  not not_1 (Zero, or_2_out);

  // Other names for the same wires on the sheet: Cin = BInvert; Op[2:0] = Operation; Result[15:0] = out_4
endmodule

module MYXOR (
  input  A,
  input  B,
  output XOR
);

  wire and_1_out, and_2_out, not_1_out, not_2_out;

  not not_1 (not_1_out, A);
  not not_2 (not_2_out, B);
  and and_1 (and_1_out, not_1_out, B);
  and and_2 (and_2_out, A, not_2_out);
  or or_1 (XOR, and_1_out, and_2_out);
endmodule

module BCD7 (
  input  A3,
  input  A2,
  input  A1,
  input  A0,
  output a,
  output b,
  output c,
  output d,
  output e,
  output f,
  output g
);

  wire and_1_out, and_2_out, and_3_out, and_4_out, and_5_out, and_6_out, and_7_out, and_8_out, and_9_out,
       and_10_out, and_11_out, and_12_out, and_13_out, and_14_out, and_15_out, and_16_out, and_17_out,
       and_18_out, and_19_out, and_20_out, and_21_out, and_22_out, and_23_out, and_24_out, and_25_out,
       and_26_out, and_27_out, and_28_out, and_29_out, and_30_out, and_31_out, and_32_out, and_33_out,
       and_34_out, and_35_out, and_36_out, and_37_out, and_38_out, and_39_out, and_40_out, and_41_out,
       and_42_out, and_43_out, and_44_out, and_45_out, and_46_out, and_47_out, not_1_out, not_2_out,
       not_3_out, not_4_out, not_5_out, not_6_out, not_7_out, not_8_out, not_9_out, not_10_out, not_11_out,
       not_12_out, not_13_out, not_14_out, not_15_out, not_16_out, not_17_out, not_18_out, not_19_out,
       not_20_out, not_21_out, not_22_out, not_23_out, not_24_out, not_25_out, not_26_out, not_27_out,
       not_28_out, not_29_out, not_30_out, not_31_out, not_32_out, not_33_out, not_34_out, not_35_out,
       not_36_out, not_37_out, not_38_out, not_39_out, not_40_out, not_41_out, not_42_out, not_43_out,
       not_44_out, not_45_out, not_46_out, not_47_out, not_48_out, not_49_out, not_50_out, not_51_out,
       not_52_out, or_1_out, or_2_out, or_3_out, or_4_out, or_5_out, or_7_out, or_9_out, or_10_out,
       or_11_out, or_12_out, or_15_out, or_16_out;

  not not_1 (not_1_out, A3);
  and and_1 (and_1_out, not_1_out, not_2_out);
  not not_2 (not_2_out, A2);
  not not_3 (not_3_out, A0);
  not not_4 (not_4_out, A3);
  not not_5 (not_5_out, A3);
  and and_2 (and_2_out, not_5_out, A2);
  and and_3 (and_3_out, A3, not_6_out);
  not not_6 (not_6_out, A2);
  not not_7 (not_7_out, A1);
  not not_8 (not_8_out, A3);
  not not_9 (not_9_out, A2);
  not not_10 (not_10_out, A3);
  and and_4 (and_4_out, not_10_out, not_11_out);
  not not_11 (not_11_out, A1);
  not not_12 (not_12_out, A0);
  not not_13 (not_13_out, A2);
  not not_14 (not_14_out, A1);
  not not_15 (not_15_out, A3);
  and and_5 (and_5_out, not_15_out, A1);
  not not_16 (not_16_out, A2);
  and and_6 (and_6_out, not_16_out, not_17_out);
  not not_17 (not_17_out, A1);
  not not_18 (not_18_out, A3);
  and and_7 (and_7_out, not_18_out, A0);
  not not_19 (not_19_out, A3);
  not not_20 (not_20_out, A3);
  and and_8 (and_8_out, not_20_out, not_21_out);
  not not_21 (not_21_out, A2);
  not not_22 (not_22_out, A0);
  not not_23 (not_23_out, A3);
  and and_9 (and_9_out, not_23_out, not_24_out);
  not not_24 (not_24_out, A2);
  not not_25 (not_25_out, A3);
  not not_26 (not_26_out, A3);
  not not_27 (not_27_out, A1);
  not not_28 (not_28_out, A2);
  not not_29 (not_29_out, A2);
  and and_10 (and_10_out, not_29_out, not_30_out);
  not not_30 (not_30_out, A1);
  not not_31 (not_31_out, A0);
  not not_32 (not_32_out, A3);
  and and_11 (and_11_out, not_32_out, A1);
  not not_33 (not_33_out, A0);
  not not_34 (not_34_out, A3);
  and and_12 (and_12_out, not_34_out, not_35_out);
  not not_35 (not_35_out, A1);
  not not_36 (not_36_out, A0);
  not not_37 (not_37_out, A3);
  and and_13 (and_13_out, not_37_out, A2);
  not not_38 (not_38_out, A1);
  not not_39 (not_39_out, A3);
  and and_14 (and_14_out, not_39_out, A2);
  not not_40 (not_40_out, A0);
  and and_15 (and_15_out, A3, not_41_out);
  not not_41 (not_41_out, A2);
  not not_42 (not_42_out, A1);
  not not_43 (not_43_out, A3);
  and and_16 (and_16_out, not_43_out, not_44_out);
  not not_44 (not_44_out, A2);
  not not_45 (not_45_out, A3);
  and and_17 (and_17_out, not_45_out, A2);
  not not_46 (not_46_out, A1);
  not not_47 (not_47_out, A3);
  and and_18 (and_18_out, not_47_out, A2);
  not not_48 (not_48_out, A0);
  and and_19 (and_19_out, A3, not_49_out);
  not not_49 (not_49_out, A2);
  not not_50 (not_50_out, A1);
  and and_20 (and_20_out, and_1_out, not_3_out);
  and and_21 (and_21_out, not_4_out, A1);
  and and_22 (and_22_out, and_2_out, A0);
  and and_23 (and_23_out, and_3_out, not_7_out);
  and and_24 (and_24_out, not_8_out, not_9_out);
  and and_25 (and_25_out, and_4_out, not_12_out);
  and and_26 (and_26_out, not_13_out, not_14_out);
  and and_27 (and_27_out, and_5_out, A0);
  or or_1 (or_1_out, and_6_out, and_7_out);
  and and_28 (and_28_out, not_19_out, A2);
  and and_29 (and_29_out, and_8_out, not_22_out);
  and and_30 (and_30_out, and_9_out, A1);
  and and_31 (and_31_out, not_25_out, A1);
  not not_51 (not_51_out, A0);
  and and_32 (and_32_out, not_26_out, A2);
  and and_33 (and_33_out, not_27_out, A0);
  and and_34 (and_34_out, A3, not_28_out);
  not not_52 (not_52_out, A1);
  and and_35 (and_35_out, and_10_out, not_31_out);
  and and_36 (and_36_out, and_11_out, not_33_out);
  and and_37 (and_37_out, and_12_out, not_36_out);
  and and_38 (and_38_out, and_13_out, not_38_out);
  and and_39 (and_39_out, and_14_out, not_40_out);
  and and_40 (and_40_out, and_15_out, not_42_out);
  and and_41 (and_41_out, and_16_out, A1);
  and and_42 (and_42_out, and_17_out, not_46_out);
  and and_43 (and_43_out, and_18_out, not_48_out);
  and and_44 (and_44_out, and_19_out, not_50_out);
  or or_2 (or_2_out, and_20_out, and_21_out);
  or or_3 (or_3_out, and_22_out, and_23_out);
  or or_4 (or_4_out, and_24_out, and_25_out);
  or or_5 (or_5_out, and_26_out, and_27_out);
  or or_6 (c, or_1_out, and_28_out);
  or or_7 (or_7_out, and_29_out, and_30_out);
  and and_45 (and_45_out, and_31_out, not_51_out);
  and and_46 (and_46_out, and_32_out, and_33_out);
  and and_47 (and_47_out, and_34_out, not_52_out);
  or or_8 (e, and_35_out, and_36_out);
  or or_9 (or_9_out, and_37_out, and_38_out);
  or or_10 (or_10_out, and_39_out, and_40_out);
  or or_11 (or_11_out, and_41_out, and_42_out);
  or or_12 (or_12_out, and_43_out, and_44_out);
  or or_13 (a, or_2_out, or_3_out);
  or or_14 (b, or_4_out, or_5_out);
  or or_15 (or_15_out, or_7_out, and_45_out);
  or or_16 (or_16_out, and_46_out, and_47_out);
  or or_17 (f, or_9_out, or_10_out);
  or or_18 (g, or_11_out, or_12_out);
  or or_19 (d, or_15_out, or_16_out);
endmodule

// Divisor
module Division (
  input  [15:0] in_1,
  output [15:0] Unidad,
  output [15:0] Decena,
  output [15:0] Centena,
  output [15:0] Unidad_de_Millar,
  output [15:0] Decena_de_Millar,
  output Signe
);

  wire [15:0] alu_16bits_1_out_4, divider_1_out, divider_2_out, divider_3_out, divider_4_out,
       multiplexer_1_out, not_1_out;

  assign not_1_out = ~in_1;  // NOT_Gate not_1, 16 bits wide
  ALU_16Bits alu_16bits_1 (
    .A(not_1_out), .Operation(3'b101), .B(16'h1), .out_4(alu_16bits_1_out_4));  // open: Overflow, Zero
  Multiplexer #(.width(16), .enable("false")) multiplexer_1 (
    .in0(in_1), .in1(alu_16bits_1_out_4), .out(multiplexer_1_out), .sel(in_1[15]));
  Divider #(.width(16)) divider_1 (.a(multiplexer_1_out), .b(16'ha), .out(divider_1_out), .rem(Unidad));  // open: upper
  Divider #(.width(16)) divider_2 (.a(divider_1_out), .b(16'ha), .out(divider_2_out), .rem(Decena));  // open: upper
  Divider #(.width(16)) divider_3 (.a(divider_2_out), .b(16'ha), .out(divider_3_out), .rem(Centena));  // open: upper
  Divider #(.width(16)) divider_4 (
    .a(divider_3_out), .b(16'ha), .out(divider_4_out), .rem(Unidad_de_Millar));  // open: upper
  Divider #(.width(16)) divider_5 (.a(divider_4_out), .b(16'ha), .rem(Decena_de_Millar));  // open: out, upper

  assign Signe = in_1[15];
endmodule

module Shifter_Dist_1 (
  input  [15:0] A,
  input  Mode,
  output [15:0] Result
);

  wire and_1_out, and_3_out, and_4_out, and_5_out, and_6_out, and_7_out, and_8_out, and_9_out, and_10_out,
       and_11_out, and_12_out, and_13_out, and_14_out, and_15_out, and_16_out, and_17_out, and_18_out,
       and_19_out, and_20_out, and_21_out, and_22_out, and_23_out, and_24_out, and_25_out, and_26_out,
       and_27_out, and_28_out, and_29_out, not_1_out;

  not not_1 (not_1_out, Mode);
  and and_1 (and_1_out, A[15], Mode);
  and and_2 (Result[15], not_1_out, A[14]);
  or or_1 (Result[14], and_1_out, and_3_out);
  and and_3 (and_3_out, not_1_out, A[13]);
  and and_4 (and_4_out, A[14], Mode);
  or or_2 (Result[13], and_4_out, and_6_out);
  and and_5 (and_5_out, A[13], Mode);
  and and_6 (and_6_out, not_1_out, A[12]);
  or or_3 (Result[12], and_5_out, and_7_out);
  and and_7 (and_7_out, not_1_out, A[11]);
  and and_8 (and_8_out, A[12], Mode);
  or or_4 (Result[11], and_8_out, and_9_out);
  and and_9 (and_9_out, not_1_out, A[10]);
  and and_10 (and_10_out, A[11], Mode);
  or or_5 (Result[10], and_10_out, and_12_out);
  and and_11 (and_11_out, A[10], Mode);
  and and_12 (and_12_out, not_1_out, A[9]);
  or or_6 (Result[9], and_11_out, and_13_out);
  and and_13 (and_13_out, not_1_out, A[8]);
  and and_14 (and_14_out, A[9], Mode);
  or or_7 (Result[8], and_14_out, and_16_out);
  and and_15 (and_15_out, A[8], Mode);
  and and_16 (and_16_out, not_1_out, A[7]);
  or or_8 (Result[7], and_15_out, and_17_out);
  and and_17 (and_17_out, not_1_out, A[6]);
  and and_18 (and_18_out, A[7], Mode);
  or or_9 (Result[6], and_18_out, and_20_out);
  and and_19 (and_19_out, A[6], Mode);
  and and_20 (and_20_out, not_1_out, A[5]);
  or or_10 (Result[5], and_19_out, and_22_out);
  and and_21 (and_21_out, A[5], Mode);
  and and_22 (and_22_out, not_1_out, A[4]);
  or or_11 (Result[4], and_21_out, and_24_out);
  and and_23 (and_23_out, A[4], Mode);
  and and_24 (and_24_out, not_1_out, A[3]);
  or or_12 (Result[3], and_23_out, and_25_out);
  and and_25 (and_25_out, not_1_out, A[2]);
  and and_26 (and_26_out, A[3], Mode);
  or or_13 (Result[2], and_26_out, and_27_out);
  and and_27 (and_27_out, not_1_out, A[1]);
  and and_28 (and_28_out, A[2], Mode);
  or or_14 (Result[1], and_28_out, and_29_out);
  and and_29 (and_29_out, not_1_out, A[0]);
  and and_30 (Result[0], A[1], Mode);
endmodule

module Shifter_Dist_2 (
  input  [15:0] A,
  input  Mode,
  output [15:0] Result
);

  wire [15:0] shifter_dist_1_1_result;

  Shifter_Dist_1 shifter_dist_1_1 (.Mode(Mode), .A(A), .Result(shifter_dist_1_1_result));
  Shifter_Dist_1 shifter_dist_1_2 (.Mode(Mode), .A(shifter_dist_1_1_result), .Result(Result));
endmodule

module Shifter_Dist_4 (
  input  [15:0] A,
  input  Mode,
  output [15:0] Result
);

  wire [15:0] shifter_dist_2_1_result;

  Shifter_Dist_2 shifter_dist_2_1 (.Mode(Mode), .A(A), .Result(shifter_dist_2_1_result));
  Shifter_Dist_2 shifter_dist_2_2 (.Mode(Mode), .A(shifter_dist_2_1_result), .Result(Result));
endmodule

module Shifter_Dist_8 (
  input  [15:0] A,
  input  Mode,
  output [15:0] Result
);

  wire [15:0] shifter_dist_4_1_result;

  Shifter_Dist_4 shifter_dist_4_1 (.Mode(Mode), .A(A), .Result(shifter_dist_4_1_result));
  Shifter_Dist_4 shifter_dist_4_2 (.Mode(Mode), .A(shifter_dist_4_1_result), .Result(Result));
endmodule

module SLR_L (
  input  [15:0] B,
  input  [15:0] A,
  input  in_3,
  output Overflow,
  output [15:0] Result
);

  wire [15:0] multiplexer_1_out, multiplexer_2_out, multiplexer_3_out, multiplexer_4_out,
       shifter_dist_1_1_result, shifter_dist_2_1_result, shifter_dist_4_1_result, shifter_dist_8_1_result;

  Shifter_Dist_1 shifter_dist_1_1 (.Mode(in_3), .A(A), .Result(shifter_dist_1_1_result));
  Multiplexer #(.width(16), .enable("false")) multiplexer_1 (
    .in0(A), .in1(shifter_dist_1_1_result), .out(multiplexer_1_out), .sel(B[0]));
  Shifter_Dist_2 shifter_dist_2_1 (.Mode(in_3), .A(multiplexer_1_out), .Result(shifter_dist_2_1_result));
  Multiplexer #(.width(16), .enable("false")) multiplexer_2 (
    .in0(multiplexer_1_out), .in1(shifter_dist_2_1_result), .out(multiplexer_2_out), .sel(B[1]));
  Shifter_Dist_4 shifter_dist_4_1 (.Mode(in_3), .A(multiplexer_2_out), .Result(shifter_dist_4_1_result));
  Multiplexer #(.width(16), .enable("false")) multiplexer_3 (
    .in0(multiplexer_2_out), .in1(shifter_dist_4_1_result), .out(multiplexer_3_out), .sel(B[2]));
  Shifter_Dist_8 shifter_dist_8_1 (.Mode(in_3), .A(multiplexer_3_out), .Result(shifter_dist_8_1_result));
  Multiplexer #(.width(16), .enable("false")) multiplexer_4 (
    .in0(multiplexer_3_out), .in1(shifter_dist_8_1_result), .out(multiplexer_4_out), .sel(B[3]));
  or or_1 (Overflow, B[4], B[5], B[6], B[7], B[8], B[9], B[10], B[11], B[12], B[13], B[14], B[15]);
  Multiplexer #(.width(16), .enable("false")) multiplexer_5 (
    .in0(multiplexer_4_out), .in1({16{1'b0}}), .out(Result), .sel(Overflow));

  // Notes on the sheet:
  //   0: Shift Logical Left
  //   1: Shift Logical Right
endmodule
