// Logisim project SLL & SLR.circ as structural Verilog: 5 circuits, main circuit Shifter Dist:1
module Shifter_Dist_1 (
  input  [15:0] A,
  input  Mode,
  output [15:0] Result
);

  wire and_2_out, and_3_out, and_4_out, and_5_out, and_6_out, and_7_out, and_8_out, and_9_out, and_10_out,
       and_11_out, and_12_out, and_13_out, and_14_out, and_15_out, and_16_out, and_17_out, and_18_out,
       and_19_out, and_20_out, and_21_out, and_22_out, and_23_out, and_24_out, and_25_out, and_26_out,
       and_27_out, and_28_out, and_30_out, not_1_out;

  not not_1 (not_1_out, Mode);
  and and_1 (Result[15], not_1_out, A[14]);
  and and_2 (and_2_out, A[15], Mode);
  or or_1 (Result[14], and_2_out, and_3_out);
  and and_3 (and_3_out, not_1_out, A[13]);
  and and_4 (and_4_out, A[14], Mode);
  or or_2 (Result[13], and_4_out, and_6_out);
  and and_5 (and_5_out, A[13], Mode);
  and and_6 (and_6_out, not_1_out, A[12]);
  or or_3 (Result[12], and_5_out, and_7_out);
  and and_7 (and_7_out, not_1_out, A[11]);
  and and_8 (and_8_out, A[12], Mode);
  or or_4 (Result[11], and_8_out, and_9_out);
  and and_9 (and_9_out, not_1_out, A[10]);
  and and_10 (and_10_out, A[11], Mode);
  or or_5 (Result[10], and_10_out, and_12_out);
  and and_11 (and_11_out, A[10], Mode);
  and and_12 (and_12_out, not_1_out, A[9]);
  or or_6 (Result[9], and_11_out, and_14_out);
  and and_13 (and_13_out, A[9], Mode);
  and and_14 (and_14_out, not_1_out, A[8]);
  or or_7 (Result[8], and_13_out, and_15_out);
  and and_15 (and_15_out, not_1_out, A[7]);
  and and_16 (and_16_out, A[8], Mode);
  or or_8 (Result[7], and_16_out, and_18_out);
  and and_17 (and_17_out, A[7], Mode);
  and and_18 (and_18_out, not_1_out, A[6]);
  or or_9 (Result[6], and_17_out, and_19_out);
  and and_19 (and_19_out, not_1_out, A[5]);
  and and_20 (and_20_out, A[6], Mode);
  or or_10 (Result[5], and_20_out, and_21_out);
  and and_21 (and_21_out, not_1_out, A[4]);
  and and_22 (and_22_out, A[5], Mode);
  or or_11 (Result[4], and_22_out, and_23_out);
  and and_23 (and_23_out, not_1_out, A[3]);
  and and_24 (and_24_out, A[4], Mode);
  or or_12 (Result[3], and_24_out, and_26_out);
  and and_25 (and_25_out, A[3], Mode);
  and and_26 (and_26_out, not_1_out, A[2]);
  or or_13 (Result[2], and_25_out, and_27_out);
  and and_27 (and_27_out, not_1_out, A[1]);
  and and_28 (and_28_out, A[2], Mode);
  or or_14 (Result[1], and_28_out, and_30_out);
  and and_29 (Result[0], A[1], Mode);
  and and_30 (and_30_out, not_1_out, A[0]);
endmodule

module Shifter_Dist_2 (
  input  [15:0] A,
  input  Mode,
  output [15:0] Result
);

  wire [15:0] shifter_dist_1_1_result;

  Shifter_Dist_1 shifter_dist_1_1 (.A(A), .Result(shifter_dist_1_1_result), .Mode(Mode));
  Shifter_Dist_1 shifter_dist_1_2 (.A(shifter_dist_1_1_result), .Result(Result), .Mode(Mode));
endmodule

module Shifter_Dist_4 (
  input  [15:0] A,
  input  Mode,
  output [15:0] Result
);

  wire [15:0] shifter_dist_2_1_result;

  Shifter_Dist_2 shifter_dist_2_1 (.A(A), .Result(shifter_dist_2_1_result), .Mode(Mode));
  Shifter_Dist_2 shifter_dist_2_2 (.A(shifter_dist_2_1_result), .Result(Result), .Mode(Mode));
endmodule

module Shifter_Dist_8 (
  input  [15:0] A,
  input  Mode,
  output [15:0] Result
);

  wire [15:0] shifter_dist_4_1_result;

  Shifter_Dist_4 shifter_dist_4_1 (.A(A), .Mode(Mode), .Result(shifter_dist_4_1_result));
  Shifter_Dist_4 shifter_dist_4_2 (.A(shifter_dist_4_1_result), .Mode(Mode), .Result(Result));
endmodule

module SLLFull (
  input  [15:0] in_1,
  input  [15:0] A,
  input  in_3,
  output [15:0] Result
);

  wire or_1_out;
  wire [15:0] multiplexer_1_out, multiplexer_2_out, multiplexer_3_out, multiplexer_4_out,
       shifter_dist_1_1_result, shifter_dist_2_1_result, shifter_dist_4_1_result, shifter_dist_8_1_result;

  Shifter_Dist_1 shifter_dist_1_1 (.A(A), .Result(shifter_dist_1_1_result), .Mode(in_3));
  Multiplexer #(.width(16), .enable("false")) multiplexer_1 (
    .in0(A), .in1(shifter_dist_1_1_result), .out(multiplexer_1_out), .sel(in_1[0]));
  Shifter_Dist_2 shifter_dist_2_1 (.A(multiplexer_1_out), .Result(shifter_dist_2_1_result), .Mode(in_3));
  Multiplexer #(.width(16), .enable("false")) multiplexer_2 (
    .in0(multiplexer_1_out), .in1(shifter_dist_2_1_result), .out(multiplexer_2_out), .sel(in_1[1]));
  Shifter_Dist_4 shifter_dist_4_1 (.A(multiplexer_2_out), .Mode(in_3), .Result(shifter_dist_4_1_result));
  Multiplexer #(.width(16), .enable("false")) multiplexer_3 (
    .in0(multiplexer_2_out), .in1(shifter_dist_4_1_result), .out(multiplexer_3_out), .sel(in_1[2]));
  Shifter_Dist_8 shifter_dist_8_1 (.A(multiplexer_3_out), .Mode(in_3), .Result(shifter_dist_8_1_result));
  Multiplexer #(.width(16), .enable("false")) multiplexer_4 (
    .in0(multiplexer_3_out), .in1(shifter_dist_8_1_result), .out(multiplexer_4_out), .sel(in_1[3]));
  or or_1 (or_1_out, in_1[4], in_1[5], in_1[6], in_1[7], in_1[8], in_1[9], in_1[10], in_1[11], in_1[12], in_1[13], in_1[14], in_1[15]);
  Multiplexer #(.width(16), .enable("false")) multiplexer_5 (
    .in0(multiplexer_4_out), .in1({16{1'b0}}), .out(Result), .sel(or_1_out));

  // Notes on the sheet:
  //   0: Shift Logical Left
  //   1: Shift Logical Right
endmodule
